# Fritzing sketch 132finprojectbread (saved by Fritzing 0.9.3b)
breadboards: 1

parts:
  Part1 = Adafruit Pi Cobbler Plus [part_number="Adafruit #2029"]
  S1 = Pushbutton [package="[THT]"]
  S2 = Pushbutton [package="[THT]"]
  S3 = Pushbutton [package="[THT]"]
  S4 = Pushbutton [package="[THT]"]
  S5 = Pushbutton [package="[THT]"]
  S6 = Pushbutton [package="[THT]"]
  S7 = Pushbutton [package="[THT]"]
  S8 = Pushbutton [package="[THT]"]

nets:
  N1: Part1.+3.3V, S1.Pin_3, S1.Pin_4, S2.Pin_3, S2.Pin_4, S3.Pin_3, S3.Pin_4, S4.Pin_3, S4.Pin_4, S5.Pin_3, S5.Pin_4, S6.Pin_3, S6.Pin_4, S7.Pin_3, S7.Pin_4, S8.Pin_3, S8.Pin_4
  N2: Part1.GPIO18, S8.Pin_1, S8.Pin_2
  N3: Part1.GPIO23, S7.Pin_1, S7.Pin_2
  N4: Part1.GPIO24, S6.Pin_1, S6.Pin_2
  N5: Part1.GPIO25, S5.Pin_1, S5.Pin_2
  N6: Part1.GPIO12, S4.Pin_1, S4.Pin_2
  N7: Part1.GPIO16, S3.Pin_1, S3.Pin_2
  N8: Part1.GPIO20, S2.Pin_1, S2.Pin_2
  N9: Part1.GPIO21, S1.Pin_1, S1.Pin_2

custom parts:
  Adafruit Pi Cobbler Plus: The Raspberry Pi B+/Pi 2/ Pi 3 has landed on the Maker World like a 40-GPIO pinned, quad-USB ported, credit card sized bomb of DIY joy. And while you can use most of our great Model B accessories by hooking up our downgrade cable, its probably a good time to upgrade your set up and accessorize using all of the Model B+'s / Pi 2's / Pi 3's 40 pins. That's why we now carry the Adafruit Assembled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
